// Logisim project CPU_Design.circ as structural Verilog
module Register_File (
  input  [3:0] RS,
  input  [3:0] RT,
  input  [3:0] RD,
  input  [15:0] Data_input
);

  wire clock_1_out, demultiplexer_1_out0, demultiplexer_1_out1, demultiplexer_1_out2, demultiplexer_1_out3,
       demultiplexer_1_out4, demultiplexer_1_out5, demultiplexer_1_out6, demultiplexer_1_out7,
       demultiplexer_1_out8, demultiplexer_1_out9, demultiplexer_1_out10, demultiplexer_1_out11,
       demultiplexer_1_out12, demultiplexer_1_out13, demultiplexer_1_out14, demultiplexer_1_out15, undriven;
  wire [15:0] multiplexer_1_out, multiplexer_2_out, Reg1_q, Reg2_q, Reg3_q, Reg4_q, Reg5_q, Reg6_q, Reg7_q,
       Reg8_q, Reg9_q, Reg10_q, Reg11_q, Reg12_q, Reg13_q, Reg14_q, Reg15_q, Reg16_q;

  Demultiplexer #(.select(4)) demultiplexer_1 (
    .out0(demultiplexer_1_out0), .out1(demultiplexer_1_out1), .out2(demultiplexer_1_out2),
    .out3(demultiplexer_1_out3), .out4(demultiplexer_1_out4), .out5(demultiplexer_1_out5),
    .out6(demultiplexer_1_out6), .out7(demultiplexer_1_out7), .out8(demultiplexer_1_out8),
    .out9(demultiplexer_1_out9), .out10(demultiplexer_1_out10), .out11(demultiplexer_1_out11),
    .out12(demultiplexer_1_out12), .out13(demultiplexer_1_out13), .out14(demultiplexer_1_out14),
    .out15(demultiplexer_1_out15), .in(undriven), .sel(RD));  // open: en
  Clock clock_1 (.out(clock_1_out));
  Register #(.width(16)) Reg1 (.D(Data_input), .en(demultiplexer_1_out0), .Q(Reg1_q), .clk(clock_1_out));  // open: clr
  Register #(.width(16)) Reg2 (.D(Data_input), .en(demultiplexer_1_out1), .Q(Reg2_q), .clk(clock_1_out));  // open: clr
  Register #(.width(16)) Reg3 (.D(Data_input), .en(demultiplexer_1_out2), .Q(Reg3_q), .clk(clock_1_out));  // open: clr
  Register #(.width(16)) Reg4 (.D(Data_input), .en(demultiplexer_1_out3), .Q(Reg4_q), .clk(clock_1_out));  // open: clr
  Register #(.width(16)) Reg5 (.D(Data_input), .en(demultiplexer_1_out4), .Q(Reg5_q), .clk(clock_1_out));  // open: clr
  Register #(.width(16)) Reg6 (.D(Data_input), .en(demultiplexer_1_out5), .Q(Reg6_q), .clk(clock_1_out));  // open: clr
  Register #(.width(16)) Reg7 (.D(Data_input), .en(demultiplexer_1_out6), .Q(Reg7_q), .clk(clock_1_out));  // open: clr
  Register #(.width(16)) Reg8 (.D(Data_input), .en(demultiplexer_1_out7), .Q(Reg8_q), .clk(clock_1_out));  // open: clr
  Register #(.width(16)) Reg9 (.D(Data_input), .en(demultiplexer_1_out8), .Q(Reg9_q), .clk(clock_1_out));  // open: clr
  Register #(.width(16)) Reg10 (
    .D(Data_input), .en(demultiplexer_1_out9), .Q(Reg10_q), .clk(clock_1_out));  // open: clr
  Register #(.width(16)) Reg11 (
    .D(Data_input), .en(demultiplexer_1_out10), .Q(Reg11_q), .clk(clock_1_out));  // open: clr
  Register #(.width(16)) Reg12 (
    .D(Data_input), .en(demultiplexer_1_out11), .Q(Reg12_q), .clk(clock_1_out));  // open: clr
  Register #(.width(16)) Reg13 (
    .D(Data_input), .en(demultiplexer_1_out12), .Q(Reg13_q), .clk(clock_1_out));  // open: clr
  Register #(.width(16)) Reg14 (
    .D(Data_input), .en(demultiplexer_1_out13), .Q(Reg14_q), .clk(clock_1_out));  // open: clr
  Register #(.width(16)) Reg15 (
    .D(Data_input), .en(demultiplexer_1_out14), .Q(Reg15_q), .clk(clock_1_out));  // open: clr
  Register #(.width(16)) Reg16 (
    .D(Data_input), .en(demultiplexer_1_out15), .Q(Reg16_q), .clk(clock_1_out));  // open: clr
  Multiplexer #(.select(4), .width(16), .enable("false")) multiplexer_1 (
    .in0(Reg1_q), .in1(Reg2_q), .in2(Reg3_q), .in3(Reg4_q), .in4(Reg5_q), .in5(Reg6_q), .in6(Reg7_q),
    .in7(Reg8_q), .in8(Reg9_q), .in9(Reg10_q), .in10(Reg11_q), .in11(Reg12_q), .in12(Reg13_q),
    .in13(Reg14_q), .in14(Reg15_q), .in15(Reg16_q), .out(multiplexer_1_out), .sel(RS));
  Multiplexer #(.select(4), .width(16), .enable("false")) multiplexer_2 (
    .in0(Reg1_q), .in1(Reg2_q), .in2(Reg3_q), .in3(Reg4_q), .in4(Reg5_q), .in5(Reg6_q), .in6(Reg7_q),
    .in7(Reg8_q), .in8(Reg9_q), .in9(Reg10_q), .in10(Reg11_q), .in11(Reg12_q), .in12(Reg13_q),
    .in13(Reg14_q), .in14(Reg15_q), .in15(Reg16_q), .out(multiplexer_2_out), .sel(RT));

  // Notes on the sheet:
  //   register write
  //   RS Out
  //   RT Out
endmodule

module ALU (
  input  [15:0] in_1,
  input  [15:0] in_2,
  input  [2:0] ALU_Op,
  output [15:0] ALU_Output,
  output greater,
  output equal
);

  wire [15:0] adder_1_out, and_1_out, divider_1_out, multiplier_1_out, or_1_out, shifter_1_out,
       shifter_2_out, subtractor_1_out;

  assign and_1_out = in_1 & in_2;  // AND_Gate and_1, 16 bits wide
  assign or_1_out = in_1 | in_2;  // OR_Gate or_1, 16 bits wide
  Adder #(.width(16)) adder_1 (.a(in_1), .b(in_2), .out(adder_1_out));  // open: cin, cout
  Subtractor #(.width(16)) subtractor_1 (.a(in_1), .b(in_2), .out(subtractor_1_out));  // open: bin, bout
  Multiplier #(.width(16)) multiplier_1 (.a(in_1), .b(in_2), .out(multiplier_1_out));  // open: cin, cout
  Divider #(.width(16)) divider_1 (.a(in_1), .b(in_2), .out(divider_1_out));  // open: upper, rem
  Shifter #(.width(16)) shifter_1 (.in(in_1), .\dist (in_2[3:0]), .out(shifter_1_out));
  Shifter #(.width(16), .shift("ar")) shifter_2 (.in(in_1), .\dist (in_2[3:0]), .out(shifter_2_out));
  Multiplexer #(.select(3), .width(16), .enable("false")) multiplexer_1 (
    .in0(and_1_out), .in1(or_1_out), .in2(adder_1_out), .in3(subtractor_1_out), .in4(multiplier_1_out),
    .in5(divider_1_out), .in6(shifter_1_out), .in7(shifter_2_out), .out(ALU_Output), .sel(ALU_Op));
  Comparator #(.width(16)) comparator_1 (.a(ALU_Output), .b({16{1'b1}}), .gt(greater), .eq(equal));  // open: lt
endmodule
